// Logisim project 1.7)  Utilisation du comparateur.circ as structural Verilog: 1 circuit, main circuit main
module main (
  input  e0,
  input  e1,
  input  e2,
  input  e3,
  output s
);

  wire [3:0] adder_1_out, not_1_out;

  not not_1 (not_1_out[0], e0);
  not not_2 (not_1_out[1], e1);
  not not_3 (not_1_out[2], e2);
  not not_4 (not_1_out[3], e3);
  Adder #(.width(4)) adder_1 (.a(not_1_out), .b(4'b0001), .out(adder_1_out));  // open: cin, cout
  Comparator #(.width(4)) comparator_1 (.a({e3, e2, e1, e0}), .b(adder_1_out), .eq(s));  // open: gt, lt
endmodule
